# Fritzing sketch Test_board (saved by Fritzing 0.9.2b)
circuit board: 6.88566cm x 5.36311cm
breadboards: 1

parts:
  U3 = SD_CARD_SOCKET_SPI [package=sdcard_spi]
  IC2 = Voltage Regulator LM1117 [package=sot223]
  C1 = Tantalum Capacitor [capacitance=10µF package="A 3216 [SMD, tantalum]"]
  U2 = ENC28J60 [package=ssop28db]
  C3 = Tantalum Capacitor [capacitance=10µF voltage=16V package="B 3528 [SMD, tantalum]"]
  R5 = Resistor [tolerance=±5% resistance=220 package="0603 [SMD]"]
  R6 = Resistor [tolerance=±5% resistance=220 package="0603 [SMD]"]
  J3 = female pin header, 6 pins [form="♀ (female)"]  # not connected
  J2 = female pin header, 10 pins [form="♀ (female)"]
  J1 = female pin header, 8 pins [form="♀ (female)"]
  J4 = female pin header, 8 pins [form="♀ (female)"]
  IC3 = Voltage Regulator LM1117 [package=sot223]
  C5 = Tantalum Capacitor [capacitance=10µF package="A 3216 [SMD, tantalum]"]
  J5 = double row female pin header, 6 pins [form="♀ (female)"]
  Y1 = CRYSTAL [package=hc49us]
  C2 = Ceramic Capacitor [capacitance=100nF package="0603 [SMD, multilayer]"]
  C6 = Ceramic Capacitor [capacitance=100nF package="0603 [SMD, multilayer]"]
  C4 = Ceramic Capacitor [capacitance=100nF package="0603 [SMD, multilayer]"]
  U1 = 74ACT125D [package=so014]
  D1 = Diode [package=sod-323]
  D2 = Diode [package=sod-323]
  D3 = Diode [package=sod-323]
  R3 = Resistor [tolerance=±5% resistance=1k package="0603 [SMD]"]
  R2 = Resistor [tolerance=±5% resistance=1k package="0603 [SMD]"]
  R1 = Resistor [tolerance=±5% resistance=1k package="0603 [SMD]"]
  R4 = Resistor [tolerance=±5% resistance=1k package="0603 [SMD]"]
  D4 = Diode [package=sod-323]
  C9 = Tantalum Capacitor [capacitance=10µF package="A 3216 [SMD, tantalum]"]
  C12 = Ceramic Capacitor [capacitance=100nF package="0603 [SMD, multilayer]"]
  C14 = Ceramic Capacitor [capacitance=100nF package="0603 [SMD, multilayer]"]
  C11 = Ceramic Capacitor [capacitance=18pF package="0603 [SMD, multilayer]"]
  C10 = Ceramic Capacitor [capacitance=18pF package="0603 [SMD, multilayer]"]
  C15 = Ceramic Capacitor [capacitance=100nF package="0603 [SMD, multilayer]"]
  C13 = Ceramic Capacitor [capacitance=100nF package="0603 [SMD, multilayer]"]
  R9 = Resistor [tolerance=±1% resistance=49.9 package="0603 [SMD]"]
  R10 = Resistor [tolerance=±1% resistance=49.9 package="0603 [SMD]"]
  R8 = Resistor [tolerance=±1% resistance=49.9 package="0603 [SMD]"]
  R7 = Resistor [tolerance=±1% resistance=49.9 package="0603 [SMD]"]
  C8 = Ceramic Capacitor [capacitance=100nF package="0603 [SMD, multilayer]"]
  C7 = Ceramic Capacitor [capacitance=100nF package="0603 [SMD, multilayer]"]
  Pad2 = Pad [width=1.7 height=1.09 connect=east]
  Pad3 = Pad [width=1.1 height=1.09 connect=center]
  RESET = Momentary Switch [package=tactile_switch_smd]
  J6 = male pin header, 3 pins [form="♂ (male)"]
  D5 = Diode [package=sma-diode_alt]
  D6 = Diode [package=sma-diode_alt]
  J7 = male pin header, 4 pins [form="♂ (male)"]
  Vin = Power Jack [package=power_jack_smd]
  F1 = Resettable Fuse PTC [package=ptc-1206]
  IC1 = V_REG_MC33269 [package=dpak]
  J8 = HANRUN RJ-45 [package=hanrun]
  10M = smd LED [color="Yellow (585nm)" package="0603 [SMD]"]
  R12 = Resistor [tolerance=±5% resistance=220 package="0603 [SMD]"]
  R13 = Resistor [tolerance=±5% resistance=220 package="0603 [SMD]"]
  Link = smd LED [color="Green (560nm)" package="0603 [SMD]"]
  R11 = Resistor [tolerance=±1% resistance=2.32k package="0603 [SMD]"]
  TP = TEST-POINT [package=pad.03x.05]
  Pad4 = Pad [width=2.1 height=1.09 connect=east]
  Pad5 = Pad [width=1.5 height=0.3 connect=east]
  Pad6 = Pad [width=1.5 height=0.3 connect=east]
  Pad7 = Pad [width=1.5 height=0.3 connect=center]
  3V3E = smd LED [color="Green (560nm)" package="0603 [SMD]"]
  R14 = Resistor [tolerance=±5% resistance=220 package="0603 [SMD]"]
  3V3S = smd LED [color="Green (560nm)" package="0603 [SMD]"]
  R15 = Resistor [tolerance=±5% resistance=220 package="0603 [SMD]"]
  5V = smd LED [color="Green (560nm)" package="0603 [SMD]"]
  R16 = Resistor [tolerance=±5% resistance=330 package="0603 [SMD]"]
  L1 = Inductor [package="0805 [SMD]"]

nets:
  N1: U3.nCS, U1.A0, D1.A, R1.Pin_0
  N2: U3.DI, U2.SI, D2.A, R2.Pin_0
  GND: U3.Vss, IC2.ADJ, C1.-, U2.VSS, U2.VSSRX, U2.VSSTX, U2.VSSPLL, U2.VSSOSC, C3.-, R5.Pin_0, R6.Pin_0, J2.pin4, J4.pin6, J4.pin7, IC3.ADJ, C5.-, J5.pin3, C2.0, C6.0, C4.0, U1.A1, U1.GND, U1.A2, C9.-, C12.0, C14.0, C11.0, C10.0, C15.0, C13.0, C8.0, C7.0, Pad2.pad, RESET.3, Vin.GND, Vin.GNDBREAK, IC1.IN, J8.GND, J8.SHIELD, R12.Pin_0, R13.Pin_0, R11.Pin_1, R14.Pin_0, R15.Pin_1, R16.Pin_1
  3.3V: U3.Vdd, IC2.OUT, C2.1, R3.Pin_1, R2.Pin_1, R1.Pin_1, 3V3S.anode
  N3: U3.CLK, U2.SCK, D3.A, R3.Pin_0
  N4: U3.DO, U1.B0
  5V: IC2.IN, C1.+, IC3.IN, C5.+, C4.1, U1.VCC, IC1.OUT, 5V.anode
  N5: U2.VCAP, C9.+
  N6: U2.CLKOUT, TP.1, Pad5.pad
  N7: U2._INT, U1.B1
  N8: U2.NC, U1.B2
  N9: U2.SO, U1.B3
  N10: U2.CS, U1.A3, R4.Pin_0, D4.A
  N11: U2.RESET, J4.pin3, J5.pin4, RESET.1
  N12: U2.TPIN-, R8.Pin_1, J8.RD-
  N13: U2.TPIN+, R7.Pin_0, J8.RD+, Pad6.pad
  N14: U2.RBIAS, R11.Pin_0
  3.1V: U2.VDDTX, U2.VDDRX, U2.VDDPLL, U2.VDDOSC, U2.VDD, IC3.OUT, C6.1, R4.Pin_1, C12.1, C14.1, C15.1, C13.1, Pad3.pad, Pad4.pad, Pad7.pad, 3V3E.anode, L1.pin_0
  N15: U2.TPOUT-, R10.Pin_1, J8.TD-
  N16: U2.TPOUT+, R9.Pin_0, J8.TD+
  N17: U2.OSC1, Y1.2, C10.1
  N18: U2.OSC2, Y1.1, C11.1
  N19: U2.LEDB, J8.YLED+, 10M.anode
  N20: U2.LEDA, J8.GLED+, Link.anode
  N21: C3.+, D5.A, D6.C, F1.2, IC1.GND
  N22: R5.Pin_1, Link.cathode
  N23: R6.Pin_1, 10M.cathode
  N24: J2.pin8, D4.C
  N25: J1.pin4, D1.C
  N26: J1.pin5, J7.pin1
  N27: J1.pin6, J7.pin3
  N28: J4.pin8, J6.pin2
  N29: J5.pin2, D2.C
  N30: J5.pin5, D3.C
  N31: J5.pin6, U1.O0, U1.O3
  N32: U1.O1, J7.pin2
  N33: U1.O2, J7.pin4
  N34: R9.Pin_1, R10.Pin_0, C8.1, J8.TDC, L1.pin_1
  N35: R8.Pin_0, R7.Pin_1, C7.1
  N36: J6.pin1, D5.C
  N37: J6.pin3, D6.A
  N38: Vin.PWR, F1.1
  N39: J8.GLED-, R13.Pin_1
  N40: J8.YLED-, R12.Pin_1
  N41: 3V3E.cathode, R14.Pin_1
  N42: 3V3S.cathode, R15.Pin_0
  N43: 5V.cathode, R16.Pin_0

notes:
  peskyToy
  HW rev. 02

custom parts:
  SD_CARD_SOCKET_SPI: SD Memory Card Connector with SPI
  HANRUN RJ-45: RJ-45 with LEDs HANRUN HR911105A
